# Fritzing sketch external-hardware-monitor (saved by Fritzing 0.9.10b)

parts:
  Bauteil1 = Arduino Nano (Rev3.0)
  Bauteil2 = Adafruit OLED Monochrome 0.91in I2C with STEMMA QT [part_number="Adafruit #4440"]

nets:
  GND: Bauteil1.GND, Bauteil2.GND
  5V: Bauteil1.5V, Bauteil2.VCC
  N1: Bauteil1.A5, Bauteil2.SCL
  N2: Bauteil1.A4, Bauteil2.SDA

custom parts:
  Adafruit OLED Monochrome 0.91in I2C with STEMMA QT: These displays are small, only about 1" diagonal, but very readable due to the high contrast of an OLED display. This display is made of 128x32 individual white OLED pixels, each one is turned on or off by the controller chip. Because the display makes its own light, no backlight is required. This reduces the power required to run the OLED and is why the display has such high contrast; we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
